# Fritzing sketch PuzzleBoxSchematic (saved by Fritzing 0.9.3b)
breadboards: 1

parts:
  Part1 = Arduino Uno (Rev3)
  R1 = Rotary Potentiometer (Small) [maximum_resistance=100kΩ package=THT]
  LCD1 = LCD screen
  J1 = Piezo Speaker
  Part2 = 9-DOF IMU L3GD20H + LSM303 [part_number=1714]
  LED1 = LED - 5mm [color="Red (633nm)" package="5 mm [THT]"]
  LED2 = LED - 5mm [color="Red (633nm)" package="5 mm [THT]"]
  LED3 = LED - 5mm [color="Red (633nm)" package="5 mm [THT]"]
  R2 = Resistor [tolerance=±5% resistance=220 package=THT]
  R3 = Resistor [tolerance=±5% resistance=220 package=THT]
  R4 = Resistor [tolerance=±5% resistance=220 package=THT]
  R5 = Resistor [tolerance=±5% resistance=1M package=THT]

nets:
  N1: Part1.A0, R5.Pin_0
  N2: Part1.A4/SDA, Part2.SDA
  N3: Part1.A5/SCL, Part2.SCL
  N4: Part1.D8, LCD1.DB5
  N5: Part1.D9_PWM, LCD1.DB4
  N6: Part1.D10_PWM/SS, LED1.anode
  N7: Part1.D11_PWM/MOSI, LED2.anode
  N8: Part1.D12/MISO, LED3.anode
  N9: Part1.D2, LCD1.E
  N10: Part1.D3_PWM, LCD1.R/W
  N11: Part1.D4, LCD1.RS
  N12: Part1.D6_PWM, LCD1.DB7
  N13: Part1.D7, LCD1.DB6
  5V: Part1.5V, R1.leg1, LCD1.VDD, LCD1.LED+, J1.pin2, Part2.VIN
  GND: Part1.GND, R1.leg2, LCD1.VSS, LCD1.LED-, Part2.GND, R2.Pin_0, R3.Pin_0, R4.Pin_0

custom parts:
  9-DOF IMU L3GD20H + LSM303: This inertial-measurement-unit combines 2 of the best quality sensors available on the market to give you 9 axes of data: 3 axes of accelerometer data, 3 axes gyroscopic, and 3 axes magnetic (compass). We tested many different 'combination' sensors and found these were the best value, with stable and reliable readings.
